# Fritzing sketch fritzing (saved by Fritzing 0.9.2b)

parts:
  Part2 = Arduino Ethernet Shield (Rev3)
  Eleman4 = RFID-RC522-v2

nets:
  N1: Part2.PWM_D11, Eleman4.MOSI
  N2: Part2.SPI/D12, Eleman4.MISO
  N3: Part2.SPI/D13, Eleman4.SCK
  N4: Part2.PWM_D6, Eleman4.RST
  N5: Part2.D7, Eleman4.SDA
  3V3: Part2.3V3, Eleman4.3.3V
  GND: Part2.GND, Eleman4.GND

custom parts:
  RFID-RC522-v2: A simple China made RFID-RC522 Reader; do check the pin labels, as this is a MFRC522 based clone.
